# Fritzing sketch CurrentTiny (saved by Fritzing 0.9.3b)
perfboards: 1

parts:
  J1 = Power Jack [package=power_jack_pth_lock]
  Part1 = ACS712 Low Current Sensor Board v12
  Part2 = FTDI Basic Programmer
  U1 = attiny85 [package=dip]
  JP1 = Header 2 [package=screwterminal-3.5mm-2_lock]

nets:
  N1: J1.GND, JP1.2
  N2: J1.PWR, Part1.IP+
  N3: Part1.IP-, JP1.1
  N4: Part1.5V, Part2.POWER, U1.Pin_8
  N5: Part1.VO, U1.Pin_3
  GND: Part1.GND, Part2.GND, U1.Pin_4
  N6: Part2.RXI, U1.Pin_7
  N7: Part2.TXO, U1.Pin_6
